# Fritzing sketch fritzing (saved by Fritzing 0.9.3b)
breadboards: 2

parts:
  Part1 = Arduino Nano (Rev3.0)
  IC1 = L293D [package=THT]
  IC2 = L293D [package=THT]
  Part2 = KY-033 Tracing Black White Line Hunting Sensor Module For Arduino
  Part3 = KY-033 Tracing Black White Line Hunting Sensor Module For Arduino
  Part4 = KY-033 Tracing Black White Line Hunting Sensor Module For Arduino
  M1 = DC Motor
  M2 = DC Motor
  M3 = DC Motor
  M4 = DC Motor
  VCC1 = 4 x AAA Battery Mount
  VCC2 = Battery block 9V

nets:
  GND: Part1.GND, IC2.0V, Part2.GND, Part3.GND, Part4.GND, VCC1.-
  N1: Part1.D2, IC2.In_1
  N2: Part1.D3, IC2.In_2
  N3: Part1.D4, IC2.In_4
  N4: Part1.D5, IC2.In_3
  N5: Part1.D6, IC1.In_1
  N6: Part1.D7, IC1.In_2
  N7: Part1.D8, IC1.In_4
  N8: Part1.D9, IC1.In_3
  N9: Part1.D10, Part4.S
  N10: Part1.D11/MOSI, Part2.S
  N11: Part1.D12/MISO, Part3.S
  N12: Part1.VIN, VCC2.+
  N13: Part1.5V, IC1.Enable_1, IC1.0V, IC1.Enable_2, IC1.+V, IC2.Enable_1, IC2.Enable_2, IC2.+V, Part2.V+, Part3.V+, Part4.V+, VCC2.-
  N14: IC1.Out_1_(_Controlled_by_Enable_1_), M4.pin_1
  N15: IC1.Out_2_(_Controlled_by_Enable_1_), M4.pin_2
  N16: IC1.+Vmotor, IC2.+Vmotor, VCC1.+
  N17: IC1.Out_3_(_Controlled_by_Enable_2_), M3.pin_2
  N18: IC1.Out_4_(_Controlled_by_Enable_2_), M3.pin_1
  N19: IC2.Out_1_(_Controlled_by_Enable_1_), M2.pin_1
  N20: IC2.Out_2_(_Controlled_by_Enable_1_), M2.pin_2
  N21: IC2.Out_3_(_Controlled_by_Enable_2_), M1.pin_2
  N22: IC2.Out_4_(_Controlled_by_Enable_2_), M1.pin_1

custom parts:
  KY-033 Tracing Black White Line Hunting Sensor Module For Arduino: Tracing Black White Line Hunting Sensor Module For Arduino Description: This is KY-033 tracking sensor. The KY-033 measures the intensity of infrared radiation and delivers it as an analog output voltage. Features: Operating voltage: 2.5 - 12V(cannot over12V) working current: 18mA-20mA at 5V Enhanced accuracy Documents: http://www.vishay.com/docs/83760/tcrt5000.pdf
